# Fritzing sketch TB2-C3-Dev-Shield-Assembly-Rev0.1 (saved by Fritzing 1.0.8)

parts:
  JL = SuperMini LEFT [package="THT; body 20.82 x 2.5 mm"]
  JR = SuperMini RIGHT [package="THT; body 20.82 x 2.5 mm"]
  J1 = 61200821621 [package="THT; body 9.0 x 17.82 mm"]
  JP1 = POWER [package="THT; 1.10 mm PCB holes"]
  R1 = 10k [package="THT axial; form leads to 7.62 mm; body max 3.7 x 2.1 mm"]
  R2 = 1k [package="THT axial; form leads to 7.62 mm; body max 3.7 x 2.1 mm"]
  D1 = WP710A10LID [package="THT; 2.54 mm pitch"]
  LEGEND = TB2 C3 DEV SHIELD / Netfreak QR / USB direction  # not connected
  LEGEND_BACK = TB2 C3 DEV SHIELD / Netfreak QR / USB direction  # not connected

nets:
  MISO: JL.1, JL.1D, J1.3
  CLK: JL.2, JL.2D, J1.6
  MOSI: JL.3, JL.3D, J1.8
  GPIO8: JL.4, JL.4D
  GPIO9: JL.5, JL.5D
  GPIO10: JL.6, JL.6D
  GPIO20: JL.7, JL.7D
  GPIO21: JL.8, JL.8D
  5V: JR.1, JR.1D
  GND: JR.2, JR.2D, J1.7
  3V3_IN: JR.3, JR.3D, JP1.1
  CS: JR.4, JR.4D, J1.1, R1.2, D1.K
  GPIO3: JR.5, JR.5D
  GPIO2: JR.6, JR.6D
  GPIO1: JR.7, JR.7D
  GPIO0: JR.8, JR.8D
  3V3_TARGET: J1.2, J1.4, J1.5, JP1.2, R1.1, R2.1
  LED_A: R2.2, D1.A

custom parts:
  SuperMini LEFT: Inner rows only; sockets open upward; 15.24 mm row spacing.
  SuperMini RIGHT: Inner rows only; sockets open upward; 15.24 mm row spacing.
  61200821621: Notch LEFT; opening UP; pin 1 at USB end. Do not fit a right-angle type.
  POWER: Fit the two-pin header only. DO NOT supply or fit a removable shunt. Leave open.
  10k: Equivalent by stated specs allowed; horizontal body; no polarity.
  1k: Equivalent by stated specs allowed; horizontal body; no polarity.
  WP710A10LID: Anode LEFT; cathode RIGHT (flat side). Mount upright; verify datasheet polarity.
